// Logisim project AGRI RAIN.circ as structural Verilog: 9 circuits, main circuit main
module main (
  input  in_1,
  input  _9,
  input  _8,
  input  _7,
  input  _6,
  input  _5,
  input  _4,
  input  _3,
  input  _2,
  input  _1,
  input  _0,
  output BUZZER,
  output LED
);

  wire bcd_to_7_segment_1_out_5, bcd_to_7_segment_1_out_6, bcd_to_7_segment_1_out_7,
       bcd_to_7_segment_1_out_8, bcd_to_7_segment_1_out_9, bcd_to_7_segment_1_out_10,
       bcd_to_7_segment_1_out_11, button_1_out, button_2_out, complement_1_out_3, complement_2_out_3,
       complement_3_out_3, complement_4_out_3, d_ff_2_qn, n16_4_1_y0, n16_4_1_y1, n16_4_1_y2, n16_4_1_y3,
       subtractor_1_s0, subtractor_1_s1, subtractor_1_s2, subtractor_1_s3;

  Button button_1 (.out(button_1_out));
  Button button_2 (.out(button_2_out));
  D_Flip_Flop d_ff_1 (.clk(button_1_out), .D(in_1), .Q(BUZZER));  // open: Qn, preset, en, reset
  D_Flip_Flop d_ff_2 (.clk(button_2_out), .D(in_1), .Q(LED), .Qn(d_ff_2_qn));  // open: preset, en, reset
  _16_4 u_16_4_1 (
    .D9(_9), .D8(_8), .D7(_7), .D6(_6), .D5(_5), .D4(_4), .D3(_3), .D2(_2), .D1(_1), .D0(_0),
    .Y3(n16_4_1_y3), .Y2(n16_4_1_y2), .Y1(n16_4_1_y1), .Y0(n16_4_1_y0), .ENABLE(d_ff_2_qn));
  complement complement_1 (.in_1(1'b0), .in_2(n16_4_1_y3), .out_3(complement_1_out_3));
  complement complement_2 (.in_1(1'b0), .in_2(n16_4_1_y2), .out_3(complement_2_out_3));
  complement complement_3 (.in_1(1'b0), .in_2(n16_4_1_y1), .out_3(complement_3_out_3));
  complement complement_4 (.in_1(1'b0), .in_2(n16_4_1_y0), .out_3(complement_4_out_3));
  SUBTRACTOR subtractor_1 (
    .in_9(1'b1), .X0(1'b0), .Y0(complement_4_out_3), .X1(1'b1), .Y1(complement_3_out_3), .X2(1'b1),
    .Y2(complement_2_out_3), .X3(1'b0), .Y3(complement_1_out_3), .s0(subtractor_1_s0), .s1(subtractor_1_s1),
    .s2(subtractor_1_s2), .s3(subtractor_1_s3));
  bcd_to_7_segment bcd_to_7_segment_1 (
    .in_1(subtractor_1_s3), .in_2(subtractor_1_s2), .in_3(subtractor_1_s1), .in_4(subtractor_1_s0),
    .out_5(bcd_to_7_segment_1_out_5), .out_6(bcd_to_7_segment_1_out_6), .out_7(bcd_to_7_segment_1_out_7),
    .out_8(bcd_to_7_segment_1_out_8), .out_9(bcd_to_7_segment_1_out_9), .out_10(bcd_to_7_segment_1_out_10),
    .out_11(bcd_to_7_segment_1_out_11));
  _7_Segment_Display u_7_segment_display_1 (
    .g(bcd_to_7_segment_1_out_11), .f(bcd_to_7_segment_1_out_10), .a(bcd_to_7_segment_1_out_5),
    .b(bcd_to_7_segment_1_out_6), .e(bcd_to_7_segment_1_out_9), .d(bcd_to_7_segment_1_out_8),
    .c(bcd_to_7_segment_1_out_7));  // open: dp

  // Notes on the sheet:
  //   RAIN SENSOR
  //   MOISTURE SENSOR INPUTS
  //   10:4 ENCODER
  //   COMPLEMENT 
  //   CALCULATION
  //   SUBTRACT BY 6
endmodule

module _4_2_encoder (
  input  in_1,
  input  in_2,
  input  in_3,
  input  in_4,
  input  in_5,
  output out_6,
  output out_7,
  output V
);

  wire nand_1_out, nand_2_out, not_1_out, not_2_out, not_3_out, not_4_out, not_5_out;

  not not_1 (not_1_out, in_1);
  not not_2 (not_2_out, in_5);
  nand nand_1 (nand_1_out, not_1_out, not_2_out, in_2);
  nand nand_2 (nand_2_out, nand_1_out, not_2_out, in_3);
  nand nand_3 (V, nand_1_out, not_2_out, not_1_out, in_4);
  not not_3 (not_3_out, not_1_out);
  not not_4 (not_4_out, nand_1_out);
  not not_5 (not_5_out, nand_2_out);
  or or_1 (out_6, not_3_out, not_4_out);
  or or_2 (out_7, not_3_out, not_5_out);
endmodule

module _16_4 (
  input  ENABLE,
  input  D9,
  input  D8,
  input  D7,
  input  D6,
  input  D5,
  input  D4,
  input  D3,
  input  D2,
  input  D1,
  input  D0,
  output Y3,
  output Y2,
  output Y1,
  output Y0
);

  wire not_1_out;

  not not_1 (not_1_out, ENABLE);
  or or_1 (Y3, D9, not_1_out, D8);
  or or_2 (Y2, D6, D7, not_1_out, D4, D5);
  or or_3 (Y1, D7, D6, not_1_out, D2, D3);
  or or_4 (Y0, D9, D7, D3, D1, not_1_out);
endmodule

module complement (
  input  in_1,
  input  in_2,
  output out_3
);

  xnor xnor_1 (out_3, in_1, in_2);
endmodule

module decoder (
  input  A0,
  input  A1,
  input  A2,
  input  A3,
  output B0,
  output B1,
  output B2,
  output B3,
  output B4,
  output B5,
  output B6,
  output B7
);

  wire not_1_out, not_2_out, not_3_out, not_4_out;

  not not_1 (not_1_out, A0);
  not not_2 (not_2_out, A1);
  not not_3 (not_3_out, A2);
  not not_4 (not_4_out, A3);
  and and_1 (B0, not_1_out, not_2_out, not_3_out, not_4_out);
  and and_2 (B1, A0, not_2_out, not_3_out, not_4_out);
  and and_3 (B2, not_1_out, not_3_out, A1, not_4_out);
  and and_4 (B3, not_3_out, A0, A1, not_4_out);
  and and_5 (B4, A2, not_1_out, not_4_out, not_2_out);
  and and_6 (B5, A2, A0, not_4_out, not_2_out);
  and and_7 (B6, A2, not_1_out, A1, not_4_out);
  and and_8 (B7, A2, A0, not_4_out, A1);
endmodule

module SUBTRACTOR (
  input  X0,
  input  Y0,
  input  X1,
  input  Y1,
  input  X2,
  input  Y2,
  input  X3,
  input  Y3,
  input  in_9,
  output s0,
  output s1,
  output s2,
  output s3
);

  wire full_adder_1_c1, full_adder_2_c1, full_adder_3_c1, xor_1_out, xor_2_out, xor_3_out, xor_4_out;

  xor xor_1 (xor_1_out, in_9, X0);
  FULL_ADDER full_adder_1 (.A(Y0), .B(xor_1_out), .C(in_9), .S(s0), .C1(full_adder_1_c1));
  xor xor_2 (xor_2_out, in_9, X1);
  FULL_ADDER full_adder_2 (.A(Y1), .B(xor_2_out), .C(full_adder_1_c1), .S(s1), .C1(full_adder_2_c1));
  xor xor_3 (xor_3_out, in_9, X2);
  FULL_ADDER full_adder_3 (.A(Y2), .B(xor_3_out), .C(full_adder_2_c1), .S(s2), .C1(full_adder_3_c1));
  xor xor_4 (xor_4_out, in_9, X3);
  FULL_ADDER full_adder_4 (.A(Y3), .B(xor_4_out), .C(full_adder_3_c1), .S(s3));  // open: C1
endmodule

module FULL_ADDER (
  input  A,
  input  B,
  input  C,
  output S,
  output C1
);

  wire and_1_out, and_2_out, xor_1_out;

  xor xor_1 (xor_1_out, A, B);
  and and_1 (and_1_out, A, B);
  xor xor_2 (S, xor_1_out, C);
  and and_2 (and_2_out, xor_1_out, C);
  or or_1 (C1, and_2_out, and_1_out);
endmodule

module bcd_to_7_segment (
  input  in_1,
  input  in_2,
  input  in_3,
  input  in_4,
  output out_5,
  output out_6,
  output out_7,
  output out_8,
  output out_9,
  output out_10,
  output out_11
);

  wire and_1_out, and_2_out, and_3_out, and_4_out, and_5_out, and_6_out, and_7_out, and_8_out, and_9_out,
       and_10_out, and_11_out, and_12_out, not_1_out, not_2_out, not_3_out, not_4_out, not_5_out, xnor_1_out,
       xor_1_out;

  not not_1 (not_1_out, in_1);
  not not_2 (not_2_out, in_2);
  not not_3 (not_3_out, in_3);
  not not_4 (not_4_out, in_4);
  and and_1 (and_1_out, not_2_out, not_4_out);
  and and_2 (and_2_out, in_2, in_4);
  not not_5 (not_5_out, not_1_out);
  xnor xnor_1 (xnor_1_out, in_3, in_4);
  and and_3 (and_3_out, not_4_out, not_2_out);
  and and_4 (and_4_out, not_2_out, in_3);
  and and_5 (and_5_out, in_2, not_3_out, in_4);
  and and_6 (and_6_out, in_3, not_4_out);
  and and_7 (and_7_out, not_2_out, not_4_out);
  and and_8 (and_8_out, in_3, not_4_out);
  and and_9 (and_9_out, in_2, not_4_out);
  and and_10 (and_10_out, not_4_out, not_3_out);
  and and_11 (and_11_out, not_3_out, in_2);
  and and_12 (and_12_out, in_2, in_2, not_4_out);
  xor xor_1 (xor_1_out, in_3, in_2);
  or or_1 (out_5, and_1_out, not_5_out, in_3, and_2_out);
  or or_2 (out_6, xnor_1_out, not_2_out);
  or or_3 (out_7, in_4, not_3_out, in_2);
  or or_4 (out_8, not_5_out, and_3_out, and_4_out, and_5_out, and_6_out);
  or or_5 (out_9, and_7_out, and_8_out);
  or or_6 (out_10, and_9_out, not_5_out, and_10_out, and_11_out);
  or or_7 (out_11, in_1, and_12_out, xor_1_out);
endmodule

module down_counter (
  input  in_1,
  input  in_2,
  input  in_3,
  input  in_4,
  input  in_5,
  output out_6,
  output out_7,
  output out_8,
  output out_9
);

  wire and_1_out, and_2_out, t_ff_1_qn, t_ff_2_qn, t_ff_3_qn;

  T_Flip_Flop t_ff_1 (.clk(in_1), .T(1'b1), .Q(out_6), .Qn(t_ff_1_qn), .reset(in_2));  // open: preset, en
  T_Flip_Flop t_ff_2 (.clk(in_1), .T(t_ff_1_qn), .Q(out_7), .Qn(t_ff_2_qn), .reset(in_3));  // open: preset, en
  and and_1 (and_1_out, t_ff_1_qn, t_ff_2_qn);
  T_Flip_Flop t_ff_3 (.clk(in_1), .T(and_1_out), .Q(out_8), .Qn(t_ff_3_qn), .reset(in_4));  // open: preset, en
  and and_2 (and_2_out, and_1_out, t_ff_3_qn);
  T_Flip_Flop t_ff_4 (.clk(in_1), .T(and_2_out), .Q(out_9), .reset(in_5));  // open: Qn, preset, en
endmodule
